# Fritzing sketch SimpleAnalogPontentiometer (saved by Fritzing 0.9.0b)
breadboards: 1

parts:
  Netduino_Plus_1 = Netduino Plus 2
  R1 = Resistor [tolerance=±5% resistance=330 package=THT]
  LED1 = LED - 5mm [color="Red (633nm)" package="5 mm [THT]"]
  R2 = Rotary Potentiometer (Small) [maximum_resistance=100kΩ package=THT]

nets:
  N1: Netduino_Plus_1.GND, R2.leg2
  N2: Netduino_Plus_1.3V3, R2.leg1
  N3: Netduino_Plus_1.A0, R2.wiper
  N4: R1.Pin_0, LED1.anode

custom parts:
  Netduino Plus 2: An open-source electronics platform using the .NET Micro Framework
